# Fritzing sketch PCB Entier (saved by Fritzing 0.9.1b)
circuit board: 3.48335cm x 20.0335cm
circuit board: 3.48335cm x 20.0335cm
breadboards: 1

parts:
  LED4 = RGB LED (com. anode, rbg) [package="5 mm [THT]"]
  LED18 = RGB LED (com. anode, rbg) [package="5 mm [THT]"]
  LED19 = RGB LED (com. anode, rbg) [package="5 mm [THT]"]
  LED23 = RGB LED (com. anode, rbg) [package="5 mm [THT]"]
  LED25 = RGB LED (com. anode, rbg) [package="5 mm [THT]"]
  J15 = female pin header, 2 pins [form="♀ (female)"]
  R1 = Resistor [tolerance=±5% resistance=220 package="0603 [SMD]"]
  R2 = Resistor [tolerance=±5% resistance=220 package="0603 [SMD]"]
  R3 = Resistor [tolerance=±5% resistance=220 package="0603 [SMD]"]
  R4 = Resistor [tolerance=±5% resistance=220 package="0603 [SMD]"]
  R5 = Resistor [tolerance=±5% resistance=220 package="0603 [SMD]"]
  R6 = Resistor [tolerance=±5% resistance=220 package="0603 [SMD]"]
  R7 = Resistor [tolerance=±5% resistance=220 package="0603 [SMD]"]
  R8 = Resistor [tolerance=±5% resistance=220 package="0603 [SMD]"]
  R18 = Resistor [tolerance=±5% resistance=220 package="0603 [SMD]"]
  R21 = Resistor [tolerance=±5% resistance=220 package="0603 [SMD]"]
  R22 = Resistor [tolerance=±5% resistance=220 package="0603 [SMD]"]
  R23 = Resistor [tolerance=±5% resistance=220 package="0603 [SMD]"]
  R25 = Resistor [tolerance=±5% resistance=220 package="0603 [SMD]"]
  U2 = 74HC595 [package="DIP16 [THT]"]
  J16 = female pin header, 3 pins [form="♀ (female)"]
  LED28 = RGB LED (com. anode, rbg) [package="5 mm [THT]"]
  LED29 = RGB LED (com. anode, rbg) [package="5 mm [THT]"]
  LED30 = RGB LED (com. anode, rbg) [package="5 mm [THT]"]
  U3 = 74HC595 [package="DIP16 [THT]"]
  R27 = Resistor [tolerance=±5% resistance=220 package="0603 [SMD]"]
  R28 = Resistor [tolerance=±5% resistance=220 package="0603 [SMD]"]
  R29 = Resistor [tolerance=±5% resistance=220 package="0603 [SMD]"]
  R30 = Resistor [tolerance=±5% resistance=220 package="0603 [SMD]"]
  R31 = Resistor [tolerance=±5% resistance=220 package="0603 [SMD]"]
  R32 = Resistor [tolerance=±5% resistance=220 package="0603 [SMD]"]
  R33 = Resistor [tolerance=±5% resistance=220 package="0603 [SMD]"]
  R34 = Resistor [tolerance=±5% resistance=220 package="0603 [SMD]"]
  R35 = Resistor [tolerance=±5% resistance=220 package="0603 [SMD]"]
  U4 = 74HC595 [package="DIP16 [THT]"]
  R38 = Resistor [tolerance=±5% resistance=220 package="0603 [SMD]"]
  R39 = Resistor [tolerance=±5% resistance=220 package="0603 [SMD]"]
  U8 = 74HC595 [package="DIP16 [THT]"]
  LED39 = RGB LED (com. anode, rbg) [package="5 mm [THT]"]
  LED40 = RGB LED (com. anode, rbg) [package="5 mm [THT]"]
  LED42 = RGB LED (com. anode, rbg) [package="5 mm [THT]"]
  LED43 = RGB LED (com. anode, rbg) [package="5 mm [THT]"]
  LED44 = RGB LED (com. anode, rbg) [package="5 mm [THT]"]
  LED45 = RGB LED (com. anode, rbg) [package="5 mm [THT]"]
  LED41 = RGB LED (com. anode, rbg) [package="5 mm [THT]"]
  R52 = Resistor [tolerance=±5% resistance=220 package=THT]
  R54 = Resistor [tolerance=±5% resistance=220 package=THT]  # not connected
  R57 = Resistor [tolerance=±5% resistance=220 package=THT]
  R58 = Resistor [tolerance=±5% resistance=220 package=THT]
  R59 = Resistor [tolerance=±5% resistance=220 package=THT]
  R60 = Resistor [tolerance=±5% resistance=220 package=THT]
  R61 = Resistor [tolerance=±5% resistance=220 package=THT]
  R62 = Resistor [tolerance=±5% resistance=220 package=THT]
  R63 = Resistor [tolerance=±5% resistance=220 package=THT]  # not connected
  R64 = Resistor [tolerance=±5% resistance=220 package=THT]
  R65 = Resistor [tolerance=±5% resistance=220 package=THT]
  R66 = Resistor [tolerance=±5% resistance=220 package=THT]
  R68 = Resistor [tolerance=±5% resistance=220 package=THT]
  R69 = Resistor [tolerance=±5% resistance=220 package=THT]  # not connected
  R70 = Resistor [tolerance=±5% resistance=220 package=THT]  # not connected
  R71 = Resistor [tolerance=±5% resistance=220 package=THT]  # not connected
  U9 = 74HC595 [package="DIP16 [THT]"]
  R72 = Resistor [tolerance=±5% resistance=220 package=THT]
  R73 = Resistor [tolerance=±5% resistance=220 package=THT]  # not connected

nets:
  N1: LED4.red_cathode, R2.Pin_0
  VCC: LED4.common_anode, LED18.common_anode, LED19.common_anode, LED23.common_anode, LED25.common_anode, J15.pin1, U2.MR, U2.VCC, LED28.common_anode, LED29.common_anode, LED30.common_anode, U3.MR, U3.VCC, U4.MR, U4.VCC
  N2: LED4.blue_cathode, R1.Pin_0
  N3: LED4.green_cathode, R3.Pin_0
  N4: LED18.red_cathode, R4.Pin_0
  N5: LED18.blue_cathode, R5.Pin_0
  N6: LED18.green_cathode, R7.Pin_0
  N7: LED19.red_cathode, R8.Pin_0
  N8: LED19.blue_cathode, R6.Pin_0
  N9: LED19.green_cathode, R35.Pin_0
  N10: LED23.red_cathode, R23.Pin_0
  N11: LED23.blue_cathode, R38.Pin_0
  N12: LED23.green_cathode, R22.Pin_0
  N13: LED25.red_cathode, R21.Pin_0
  N14: LED25.blue_cathode, R39.Pin_0
  N15: LED25.green_cathode, R25.Pin_0
  GND: J15.pin2, U2.GND, U2.OE, U3.GND, U3.OE, U4.GND, U4.OE
  N16: R1.Pin_1, U2.Q5
  N17: R2.Pin_1, U2.Q0
  N18: R3.Pin_1, U2.Q6
  N19: R4.Pin_1, U2.Q7
  N20: R5.Pin_1, U2.Q4
  N21: R6.Pin_1, U2.Q1
  N22: R7.Pin_1, U2.Q3
  N23: R8.Pin_1, U2.Q2
  N24: R18.Pin_0, LED30.green_cathode
  N25: R18.Pin_1, U4.Q5
  N26: R21.Pin_1, U4.Q3
  N27: R22.Pin_1, U4.Q7
  N28: R23.Pin_1, U4.Q4
  N29: R25.Pin_1, U4.Q1
  N30: U2.Q7', U3.DS
  N31: U2.SH_CP, J16.pin1, U3.SH_CP, U4.SH_CP
  N32: U2.ST_CP, J16.pin2, U3.ST_CP, U4.ST_CP
  N33: U2.DS, J16.pin3
  N34: LED28.red_cathode, R30.Pin_0
  N35: LED28.blue_cathode, R27.Pin_0
  N36: LED28.green_cathode, R29.Pin_0
  N37: LED29.red_cathode, R34.Pin_0
  N38: LED29.blue_cathode, R33.Pin_0
  N39: LED29.green_cathode, R31.Pin_0
  N40: LED30.red_cathode, R32.Pin_0
  N41: LED30.blue_cathode, R28.Pin_0
  N42: U3.Q1, R32.Pin_1
  N43: U3.Q2, R31.Pin_1
  N44: U3.Q3, R33.Pin_1
  N45: U3.Q4, R30.Pin_1
  N46: U3.Q5, R27.Pin_1
  N47: U3.Q6, R29.Pin_1
  N48: U3.Q7, R34.Pin_1
  N49: U3.Q7', U4.DS
  N50: U3.Q0, R35.Pin_1
  N51: R28.Pin_1, U4.Q0
  N52: U4.Q2, R39.Pin_1
  N53: U4.Q6, R38.Pin_1
  N54: U8.Q1, R59.Pin_1
  N55: U8.Q2, R57.Pin_1
  N56: U8.Q3, R60.Pin_0
  N57: U8.Q4, R61.Pin_0
  N58: U8.Q6, R62.Pin_0
  N59: U8.Q7, R66.Pin_0
  N60: U8.Q0, R58.Pin_0
  N61: LED39.blue_cathode, R66.Pin_1
  N62: LED40.red_cathode, R60.Pin_1
  N63: LED40.blue_cathode, R68.Pin_0
  N64: LED40.green_cathode, R58.Pin_1
  N65: LED42.blue_cathode, R62.Pin_1
  N66: LED42.green_cathode, R65.Pin_0
  N67: LED43.green_cathode, R59.Pin_0
  N68: LED44.green_cathode, R57.Pin_0
  N69: LED45.blue_cathode, R52.Pin_0
  N70: LED41.blue_cathode, R61.Pin_1
  N71: LED41.green_cathode, R64.Pin_0
  N72: U9.Q0, R72.Pin_0
