# Fritzing sketch PCB Entier (saved by Fritzing 0.9.1b)
circuit board: 3.53266cm x 20.0335cm
breadboards: 1

parts:
  LED4 = RGB LED (com. anode, rbg) [package="5 mm [THT]"]
  LED18 = RGB LED (com. anode, rbg) [package="5 mm [THT]"]
  LED19 = RGB LED (com. anode, rbg) [package="5 mm [THT]"]
  LED23 = RGB LED (com. anode, rbg) [package="5 mm [THT]"]  # not connected
  LED25 = RGB LED (com. anode, rbg) [package="5 mm [THT]"]  # not connected
  LED26 = RGB LED (com. anode, rbg) [package="5 mm [THT]"]  # not connected
  LED27 = RGB LED (com. anode, rbg) [package="5 mm [THT]"]  # not connected
  J15 = female pin header, 2 pins [form="♀ (female)"]
  R1 = Resistor [tolerance=±5% resistance=220 package="0603 [SMD]"]
  R2 = Resistor [tolerance=±5% resistance=220 package="0603 [SMD]"]
  R3 = Resistor [tolerance=±5% resistance=220 package="0603 [SMD]"]
  R4 = Resistor [tolerance=±5% resistance=220 package="0603 [SMD]"]
  R5 = Resistor [tolerance=±5% resistance=220 package="0603 [SMD]"]
  R6 = Resistor [tolerance=±5% resistance=220 package="0603 [SMD]"]
  R7 = Resistor [tolerance=±5% resistance=220 package="0603 [SMD]"]
  R8 = Resistor [tolerance=±5% resistance=220 package="0603 [SMD]"]
  R18 = Resistor [tolerance=±5% resistance=220 package="0603 [SMD]"]  # not connected
  R20 = Resistor [tolerance=±5% resistance=220 package="0603 [SMD]"]  # not connected
  R21 = Resistor [tolerance=±5% resistance=220 package="0603 [SMD]"]  # not connected
  R22 = Resistor [tolerance=±5% resistance=220 package="0603 [SMD]"]  # not connected
  R23 = Resistor [tolerance=±5% resistance=220 package="0603 [SMD]"]  # not connected
  R24 = Resistor [tolerance=±5% resistance=220 package="0603 [SMD]"]  # not connected
  R25 = Resistor [tolerance=±5% resistance=220 package="0603 [SMD]"]  # not connected
  R26 = Resistor [tolerance=±5% resistance=220 package="0603 [SMD]"]  # not connected
  U2 = 74HC595 [package="DIP16 [THT]"]
  J16 = female pin header, 3 pins [form="♀ (female)"]
  LED28 = RGB LED (com. anode, rbg) [package="5 mm [THT]"]
  LED29 = RGB LED (com. anode, rbg) [package="5 mm [THT]"]
  LED30 = RGB LED (com. anode, rbg) [package="5 mm [THT]"]
  U3 = 74HC595 [package="DIP16 [THT]"]
  R27 = Resistor [tolerance=±5% resistance=220 package="0603 [SMD]"]
  R28 = Resistor [tolerance=±5% resistance=220 package="0603 [SMD]"]
  R29 = Resistor [tolerance=±5% resistance=220 package="0603 [SMD]"]
  R30 = Resistor [tolerance=±5% resistance=220 package="0603 [SMD]"]
  R31 = Resistor [tolerance=±5% resistance=220 package="0603 [SMD]"]
  R32 = Resistor [tolerance=±5% resistance=220 package="0603 [SMD]"]
  R33 = Resistor [tolerance=±5% resistance=220 package="0603 [SMD]"]
  R34 = Resistor [tolerance=±5% resistance=220 package="0603 [SMD]"]
  R35 = Resistor [tolerance=±5% resistance=220 package="0603 [SMD]"]

nets:
  N1: LED4.red_cathode, R2.Pin_0
  VCC: LED4.common_anode, LED18.common_anode, LED19.common_anode, J15.pin1, U2.MR, U2.VCC, U3.MR, U3.VCC
  N2: LED4.blue_cathode, R1.Pin_0
  N3: LED4.green_cathode, R3.Pin_0
  N4: LED18.red_cathode, R4.Pin_0
  N5: LED18.blue_cathode, R5.Pin_0
  N6: LED18.green_cathode, R7.Pin_0
  N7: LED19.red_cathode, R8.Pin_0
  N8: LED19.blue_cathode, R6.Pin_0
  N9: LED19.green_cathode, R35.Pin_0
  GND: J15.pin2, U2.GND, U2.OE, U3.GND, U3.OE
  N10: R1.Pin_1, U2.Q5
  N11: R2.Pin_1, U2.Q0
  N12: R3.Pin_1, U2.Q6
  N13: R4.Pin_1, U2.Q7
  N14: R5.Pin_1, U2.Q4
  N15: R6.Pin_1, U2.Q1
  N16: R7.Pin_1, U2.Q3
  N17: R8.Pin_1, U2.Q2
  N18: U2.Q7', U3.DS
  N19: U2.SH_CP, J16.pin1, U3.SH_CP
  N20: U2.ST_CP, J16.pin2, U3.ST_CP
  N21: U2.DS, J16.pin3
  N22: LED28.red_cathode, R30.Pin_0
  N23: LED28.blue_cathode, R27.Pin_0
  N24: LED28.green_cathode, R29.Pin_0
  N25: LED29.red_cathode, R34.Pin_0
  N26: LED29.blue_cathode, R33.Pin_0
  N27: LED29.green_cathode, R31.Pin_0
  N28: LED30.red_cathode, R32.Pin_0
  N29: LED30.blue_cathode, R28.Pin_0
  N30: U3.Q1, R32.Pin_1
  N31: U3.Q2, R31.Pin_1
  N32: U3.Q3, R33.Pin_1
  N33: U3.Q4, R30.Pin_1
  N34: U3.Q5, R27.Pin_1
  N35: U3.Q6, R29.Pin_1
  N36: U3.Q7, R34.Pin_1
  N37: U3.Q0, R35.Pin_1
