# Fritzing sketch PCB Entier (saved by Fritzing 0.9.1b)
circuit board: 3.46923cm x 20.2382cm
circuit board: 3.48335cm x 20.0335cm
breadboards: 1

parts:
  LED4 = RGB LED (com. anode, rbg) [package="5 mm [THT]"]
  LED18 = RGB LED (com. anode, rbg) [package="5 mm [THT]"]
  LED19 = RGB LED (com. anode, rbg) [package="5 mm [THT]"]
  LED23 = RGB LED (com. anode, rbg) [package="5 mm [THT]"]
  LED25 = RGB LED (com. anode, rbg) [package="5 mm [THT]"]
  J15 = female pin header, 2 pins [form="♀ (female)"]
  R1 = Resistor [tolerance=±5% resistance=220 package="0603 [SMD]"]
  R2 = Resistor [tolerance=±5% resistance=220 package="0603 [SMD]"]
  R3 = Resistor [tolerance=±5% resistance=220 package="0603 [SMD]"]
  R4 = Resistor [tolerance=±5% resistance=220 package="0603 [SMD]"]
  R5 = Resistor [tolerance=±5% resistance=220 package="0603 [SMD]"]
  R6 = Resistor [tolerance=±5% resistance=220 package="0603 [SMD]"]
  R7 = Resistor [tolerance=±5% resistance=220 package="0603 [SMD]"]
  R8 = Resistor [tolerance=±5% resistance=220 package="0603 [SMD]"]
  R18 = Resistor [tolerance=±5% resistance=220 package="0603 [SMD]"]
  R21 = Resistor [tolerance=±5% resistance=220 package="0603 [SMD]"]
  R22 = Resistor [tolerance=±5% resistance=220 package="0603 [SMD]"]
  R23 = Resistor [tolerance=±5% resistance=220 package="0603 [SMD]"]
  R25 = Resistor [tolerance=±5% resistance=220 package="0603 [SMD]"]
  U2 = 74HC595 [package="DIP16 [THT]"]
  J16 = female pin header, 3 pins [form="♀ (female)"]
  LED28 = RGB LED (com. anode, rbg) [package="5 mm [THT]"]
  LED29 = RGB LED (com. anode, rbg) [package="5 mm [THT]"]
  LED30 = RGB LED (com. anode, rbg) [package="5 mm [THT]"]
  U3 = 74HC595 [package="DIP16 [THT]"]
  R27 = Resistor [tolerance=±5% resistance=220 package="0603 [SMD]"]
  R28 = Resistor [tolerance=±5% resistance=220 package="0603 [SMD]"]
  R29 = Resistor [tolerance=±5% resistance=220 package="0603 [SMD]"]
  R30 = Resistor [tolerance=±5% resistance=220 package="0603 [SMD]"]
  R31 = Resistor [tolerance=±5% resistance=220 package="0603 [SMD]"]
  R32 = Resistor [tolerance=±5% resistance=220 package="0603 [SMD]"]
  R33 = Resistor [tolerance=±5% resistance=220 package="0603 [SMD]"]
  R34 = Resistor [tolerance=±5% resistance=220 package="0603 [SMD]"]
  R35 = Resistor [tolerance=±5% resistance=220 package="0603 [SMD]"]
  U4 = 74HC595 [package="DIP16 [THT]"]
  R38 = Resistor [tolerance=±5% resistance=220 package="0603 [SMD]"]
  R39 = Resistor [tolerance=±5% resistance=220 package="0603 [SMD]"]
  U8 = 74HC595 [package="DIP16 [THT]"]
  LED39 = RGB LED (com. anode, rbg) [package="5 mm [THT]"]
  LED42 = RGB LED (com. anode, rbg) [package="5 mm [THT]"]
  LED44 = RGB LED (com. anode, rbg) [package="5 mm [THT]"]
  LED45 = RGB LED (com. anode, rbg) [package="5 mm [THT]"]
  LED41 = RGB LED (com. anode, rbg) [package="5 mm [THT]"]
  R57 = Resistor [tolerance=±5% resistance=220 package=THT]
  R63 = Resistor [tolerance=±5% resistance=220 package=THT]
  R66 = Resistor [tolerance=±5% resistance=220 package=THT]
  R69 = Resistor [tolerance=±5% resistance=220 package=THT]
  R70 = Resistor [tolerance=±5% resistance=220 package=THT]
  U9 = 74HC595 [package="DIP16 [THT]"]
  R78 = Resistor [tolerance=±5% resistance=220 package=THT]
  J18 = female pin header, 2 pins [form="♀ (female)"]
  J17 = female pin header, 3 pins [form="♀ (female)"]
  R79 = Resistor [tolerance=±5% resistance=220 package=THT]
  R80 = Resistor [tolerance=±5% resistance=220 package=THT]
  R81 = Resistor [tolerance=±5% resistance=220 package=THT]
  R82 = Resistor [tolerance=±5% resistance=220 package=THT]
  LED40 = RGB LED (com. anode, rbg) [package="5 mm [THT]"]
  R83 = Resistor [tolerance=±5% resistance=220 package=THT]
  R84 = Resistor [tolerance=±5% resistance=220 package=THT]
  R85 = Resistor [tolerance=±5% resistance=220 package=THT]
  R86 = Resistor [tolerance=±5% resistance=220 package=THT]
  R87 = Resistor [tolerance=±5% resistance=220 package=THT]
  R88 = Resistor [tolerance=±5% resistance=220 package=THT]
  R89 = Resistor [tolerance=±5% resistance=220 package=THT]
  U10 = 74HC595 [package="DIP16 [THT]"]
  U11 = 74HC595 [package="DIP16 [THT]"]
  LED46 = RGB LED (com. anode, rbg) [package="5 mm [THT]"]
  LED48 = RGB LED (com. anode, rbg) [package="5 mm [THT]"]
  LED49 = RGB LED (com. anode, rbg) [package="5 mm [THT]"]
  LED50 = RGB LED (com. anode, rbg) [package="5 mm [THT]"]
  LED51 = RGB LED (com. anode, rbg) [package="5 mm [THT]"]
  R92 = Resistor [tolerance=±5% resistance=220 package=THT]  # not connected
  R93 = Resistor [tolerance=±5% resistance=220 package=THT]
  R95 = Resistor [tolerance=±5% resistance=220 package=THT]
  R97 = Resistor [tolerance=±5% resistance=220 package=THT]
  R100 = Resistor [tolerance=±5% resistance=220 package=THT]
  R101 = Resistor [tolerance=±5% resistance=220 package=THT]
  R102 = Resistor [tolerance=±5% resistance=220 package=THT]
  R103 = Resistor [tolerance=±5% resistance=220 package=THT]
  R104 = Resistor [tolerance=±5% resistance=220 package=THT]
  R105 = Resistor [tolerance=±5% resistance=220 package=THT]
  R106 = Resistor [tolerance=±5% resistance=220 package=THT]  # not connected
  R107 = Resistor [tolerance=±5% resistance=220 package=THT]
  R108 = Resistor [tolerance=±5% resistance=220 package=THT]
  R109 = Resistor [tolerance=±5% resistance=220 package=THT]
  R110 = Resistor [tolerance=±5% resistance=220 package=THT]  # not connected
  R111 = Resistor [tolerance=±5% resistance=220 package=THT]
  R112 = Resistor [tolerance=±5% resistance=220 package=THT]
  R113 = Resistor [tolerance=±5% resistance=220 package=THT]
  R114 = Resistor [tolerance=±5% resistance=220 package=THT]

nets:
  N1: LED4.red_cathode, R2.Pin_0
  VCC: LED4.common_anode, LED18.common_anode, LED19.common_anode, LED23.common_anode, LED25.common_anode, J15.pin1, U2.MR, U2.VCC, LED28.common_anode, LED29.common_anode, LED30.common_anode, U3.MR, U3.VCC, U4.MR, U4.VCC
  N2: LED4.blue_cathode, R1.Pin_0
  N3: LED4.green_cathode, R3.Pin_0
  N4: LED18.red_cathode, R4.Pin_0
  N5: LED18.blue_cathode, R5.Pin_0
  N6: LED18.green_cathode, R7.Pin_0
  N7: LED19.red_cathode, R8.Pin_0
  N8: LED19.blue_cathode, R6.Pin_0
  N9: LED19.green_cathode, R35.Pin_0
  N10: LED23.red_cathode, R23.Pin_0
  N11: LED23.blue_cathode, R38.Pin_0
  N12: LED23.green_cathode, R22.Pin_0
  N13: LED25.red_cathode, R21.Pin_0
  N14: LED25.blue_cathode, R39.Pin_0
  N15: LED25.green_cathode, R25.Pin_0
  GND: J15.pin2, U2.GND, U2.OE, U3.GND, U3.OE, U4.GND, U4.OE
  N16: R1.Pin_1, U2.Q5
  N17: R2.Pin_1, U2.Q0
  N18: R3.Pin_1, U2.Q6
  N19: R4.Pin_1, U2.Q7
  N20: R5.Pin_1, U2.Q4
  N21: R6.Pin_1, U2.Q1
  N22: R7.Pin_1, U2.Q3
  N23: R8.Pin_1, U2.Q2
  N24: R18.Pin_0, LED30.green_cathode
  N25: R18.Pin_1, U4.Q5
  N26: R21.Pin_1, U4.Q3
  N27: R22.Pin_1, U4.Q7
  N28: R23.Pin_1, U4.Q4
  N29: R25.Pin_1, U4.Q1
  N30: U2.Q7', U3.DS
  N31: U2.SH_CP, J16.pin1, U3.SH_CP, U4.SH_CP
  N32: U2.ST_CP, J16.pin2, U3.ST_CP, U4.ST_CP
  N33: U2.DS, J16.pin3
  N34: LED28.red_cathode, R30.Pin_0
  N35: LED28.blue_cathode, R27.Pin_0
  N36: LED28.green_cathode, R29.Pin_0
  N37: LED29.red_cathode, R34.Pin_0
  N38: LED29.blue_cathode, R33.Pin_0
  N39: LED29.green_cathode, R31.Pin_0
  N40: LED30.red_cathode, R32.Pin_0
  N41: LED30.blue_cathode, R28.Pin_0
  N42: U3.Q1, R32.Pin_1
  N43: U3.Q2, R31.Pin_1
  N44: U3.Q3, R33.Pin_1
  N45: U3.Q4, R30.Pin_1
  N46: U3.Q5, R27.Pin_1
  N47: U3.Q6, R29.Pin_1
  N48: U3.Q7, R34.Pin_1
  N49: U3.Q7', U4.DS
  N50: U3.Q0, R35.Pin_1
  N51: R28.Pin_1, U4.Q0
  N52: U4.Q2, R39.Pin_1
  N53: U4.Q6, R38.Pin_1
  N54: U8.Q1, R100.Pin_0
  N55: U8.Q2, R87.Pin_0
  N56: U8.Q3, R78.Pin_1
  N57: U8.Q4, R57.Pin_1
  N58: U8.Q5, R79.Pin_0
  N59: U8.Q6, R66.Pin_0
  N60: U8.Q7, R63.Pin_0
  GND_2: U8.GND, U8.OE, LED39.common_anode, LED42.common_anode, LED44.common_anode, LED45.common_anode, LED41.common_anode, U9.GND, U9.OE, J18.pin1, LED40.common_anode, U10.GND, U11.GND, LED46.common_anode, LED48.common_anode, LED49.common_anode, LED50.common_anode, LED51.common_anode
  VCC_2: U8.MR, U8.VCC, U9.MR, U9.VCC, J18.pin2
  N61: U8.SH_CP, U9.SH_CP, J17.pin3, U10.SH_CP, U11.SH_CP
  N62: U8.ST_CP, U9.ST_CP, J17.pin2, U10.ST_CP, U11.ST_CP
  N63: U8.Q0, R88.Pin_1
  N64: LED39.red_cathode, R80.Pin_0
  N65: LED39.blue_cathode, R83.Pin_0
  N66: LED39.green_cathode, R63.Pin_1
  N67: LED42.red_cathode, R81.Pin_0
  N68: LED42.blue_cathode, R84.Pin_0
  N69: LED42.green_cathode, R66.Pin_1
  N70: LED44.red_cathode, R111.Pin_0
  N71: LED44.blue_cathode, R70.Pin_0
  N72: LED44.green_cathode, R78.Pin_0
  N73: LED45.red_cathode, R89.Pin_1
  N74: LED45.blue_cathode, R69.Pin_0
  N75: LED45.green_cathode, R57.Pin_0
  N76: LED41.red_cathode, R82.Pin_0
  N77: LED41.blue_cathode, R85.Pin_0
  N78: LED41.green_cathode, R79.Pin_1
  N79: R69.Pin_1, R112.Pin_0
  N80: R70.Pin_1, U11.Q1
  N81: U9.Q1, R84.Pin_1
  N82: U9.Q2, R85.Pin_1
  N83: U9.Q3, R83.Pin_1
  N84: U9.Q4, R80.Pin_1
  N85: U9.Q5, R81.Pin_1
  N86: U9.Q6, R86.Pin_1
  N87: U9.Q7, R89.Pin_0
  N88: U9.DS, J17.pin1
  N89: U9.Q0, R82.Pin_1
  N90: LED40.red_cathode, R87.Pin_1
  N91: LED40.blue_cathode, R86.Pin_0
  N92: LED40.green_cathode, R88.Pin_0
  N93: U10.Q1, R109.Pin_0
  N94: U10.Q2, R101.Pin_0
  N95: U10.Q3, R114.Pin_1
  N96: U10.Q4, R113.Pin_1
  N97: U10.Q5, R102.Pin_1
  N98: U10.Q6, R108.Pin_1
  N99: U10.Q7, R95.Pin_0
  N100: U10.Q0, R104.Pin_1
  N101: U11.Q2, R105.Pin_1
  N102: U11.Q3, R112.Pin_1
  N103: U11.Q4, R111.Pin_1
  N104: U11.Q5, R107.Pin_1
  N105: U11.Q6, R97.Pin_1
  N106: U11.Q7, R93.Pin_0
  N107: U11.Q0, R103.Pin_1
  N108: LED46.red_cathode, R107.Pin_0
  N109: LED46.blue_cathode, R105.Pin_0
  N110: LED46.green_cathode, R100.Pin_1
  N111: LED48.red_cathode, R93.Pin_1
  N112: LED48.green_cathode, R102.Pin_0
  N113: LED49.red_cathode, R109.Pin_1
  N114: LED49.blue_cathode, R114.Pin_0
  N115: LED49.green_cathode, R113.Pin_0
  N116: LED50.red_cathode, R103.Pin_0
  N117: LED50.blue_cathode, R97.Pin_0
  N118: LED50.green_cathode, R95.Pin_1
  N119: LED51.red_cathode, R101.Pin_1
  N120: LED51.blue_cathode, R108.Pin_0
  N121: LED51.green_cathode, R104.Pin_0
