# Fritzing sketch PCB Led Drivers compressed before dupli (saved by Fritzing 0.9.1b)
circuit board: 3.15899cm x 40.09cm
breadboards: 1

parts:
  J15 = female pin header, 2 pins [form="♀ (female)"]  # not connected
  J16 = female pin header, 3 pins [form="♀ (female)"]  # not connected
  C5 = Tantalum Capacitor [capacitance=1μF package="100 mil [THT, tantalum]"]
  C6 = Ceramic Capacitor [capacitance=100nF package="100 mil [THT, multilayer]"]
  LED28 = RGB LED (com. anode, rbg) [package="5 mm [THT]"]
  LED29 = RGB LED (com. anode, rbg) [package="5 mm [THT]"]
  LED30 = RGB LED (com. anode, rbg) [package="5 mm [THT]"]
  LED31 = RGB LED (com. anode, rbg) [package="5 mm [THT]"]
  LED32 = RGB LED (com. anode, rbg) [package="5 mm [THT]"]
  LED33 = RGB LED (com. anode, rbg) [package="5 mm [THT]"]
  R43 = Resistor [tolerance=±5% resistance=220 package=THT]
  R44 = Resistor [tolerance=±5% resistance=220 package=THT]
  IC4 = IC, DIP package, 16 pins [chip_label=IC]
  IC5 = IC, DIP package, 16 pins [chip_label=IC]
  C7 = Tantalum Capacitor [capacitance=1μF package="100 mil [THT, tantalum]"]
  C8 = Tantalum Capacitor [capacitance=1μF package="100 mil [THT, tantalum]"]
  C9 = Ceramic Capacitor [capacitance=100nF package="100 mil [THT, multilayer]"]
  C10 = Ceramic Capacitor [capacitance=100nF package="100 mil [THT, multilayer]"]
  LED34 = RGB LED (com. anode, rbg) [package="5 mm [THT]"]
  LED36 = RGB LED (com. anode, rbg) [package="5 mm [THT]"]
  R45 = Resistor [tolerance=±5% resistance=220 package=THT]
  IC6 = IC, DIP package, 16 pins [chip_label=IC]

nets:
  N1: C5.-, C6.1, R43.Pin_1, R44.Pin_1, IC4.pin1, IC4.pin13, IC5.pin1, IC5.pin13, C7.-, C8.-, C9.1, C10.1, R45.Pin_1, IC6.pin1, IC6.pin13
  N2: C5.+, C6.0, LED28.common_anode, LED29.common_anode, LED30.common_anode, LED31.common_anode, LED32.common_anode, LED33.common_anode, LED34.common_anode, LED36.common_anode
  N3: LED28.red_cathode, IC5.pin6
  N4: LED28.blue_cathode, IC5.pin7
  N5: LED28.green_cathode, IC5.pin8
  N6: LED29.red_cathode, IC4.pin11
  N7: LED29.blue_cathode, IC4.pin12
  N8: LED29.green_cathode, IC5.pin5
  N9: LED30.red_cathode, IC5.pin12
  N10: LED30.blue_cathode, IC6.pin5
  N11: LED30.green_cathode, IC6.pin6
  N12: LED31.red_cathode, IC4.pin8
  N13: LED31.blue_cathode, IC4.pin9
  N14: LED31.green_cathode, IC4.pin10
  N15: LED32.red_cathode, IC5.pin9
  N16: LED32.blue_cathode, IC5.pin10
  N17: LED32.green_cathode, IC5.pin11
  N18: LED33.red_cathode, IC4.pin5
  N19: LED33.blue_cathode, IC4.pin6
  N20: LED33.green_cathode, IC4.pin7
  N21: R43.Pin_0, IC4.pin15
  N22: R44.Pin_0, IC5.pin15
  N23: IC4.pin3, IC5.pin3, IC6.pin3
  N24: IC4.pin14, IC5.pin2
  N25: IC4.pin16, IC5.pin16, C7.+, C8.+, C9.0, C10.0, IC6.pin16
  N26: IC5.pin4, IC6.pin4
  N27: IC5.pin14, IC6.pin2
  N28: LED34.red_cathode, IC6.pin7
  N29: LED34.blue_cathode, IC6.pin8
  N30: LED34.green_cathode, IC6.pin9
  N31: LED36.red_cathode, IC6.pin10
  N32: LED36.blue_cathode, IC6.pin11
  N33: LED36.green_cathode, IC6.pin12
  N34: R45.Pin_0, IC6.pin15

notes:
  +
  -
  le
  clk
  sd
