# Fritzing sketch PCB Led Drivers horizontaux (saved by Fritzing 0.9.1b)
circuit board: 3.15899cm x 19.9923cm
breadboards: 1

parts:
  LED4 = RGB LED (com. anode, rbg) [package="5 mm [THT]"]
  LED18 = RGB LED (com. anode, rbg) [package="5 mm [THT]"]
  LED19 = RGB LED (com. anode, rbg) [package="5 mm [THT]"]
  J15 = female pin header, 2 pins [form="♀ (female)"]
  J16 = female pin header, 3 pins [form="♀ (female)"]
  R40 = Resistor [tolerance=±5% resistance=220 package=THT]
  IC1 = IC, DIP package, 16 pins [chip_label=IC]
  C1 = Tantalum Capacitor [capacitance=1μF package="100 mil [THT, tantalum]"]
  C2 = Ceramic Capacitor [capacitance=100nF package="100 mil [THT, multilayer]"]
  LED21 = RGB LED (com. anode, rbg) [package="5 mm [THT]"]
  LED23 = RGB LED (com. anode, rbg) [package="5 mm [THT]"]
  LED24 = RGB LED (com. anode, rbg) [package="5 mm [THT]"]
  R41 = Resistor [tolerance=±5% resistance=220 package=THT]
  IC2 = IC, DIP package, 16 pins [chip_label=IC]
  C3 = Tantalum Capacitor [capacitance=1μF package="100 mil [THT, tantalum]"]
  C4 = Ceramic Capacitor [capacitance=100nF package="100 mil [THT, multilayer]"]
  LED25 = RGB LED (com. anode, rbg) [package="5 mm [THT]"]
  LED27 = RGB LED (com. anode, rbg) [package="5 mm [THT]"]
  R42 = Resistor [tolerance=±5% resistance=220 package=THT]
  IC3 = IC, DIP package, 16 pins [chip_label=IC]
  C5 = Tantalum Capacitor [capacitance=1μF package="100 mil [THT, tantalum]"]
  C6 = Ceramic Capacitor [capacitance=100nF package="100 mil [THT, multilayer]"]
  LED28 = RGB LED (com. anode, rbg) [package="5 mm [THT]"]
  LED29 = RGB LED (com. anode, rbg) [package="5 mm [THT]"]
  LED30 = RGB LED (com. anode, rbg) [package="5 mm [THT]"]
  LED31 = RGB LED (com. anode, rbg) [package="5 mm [THT]"]
  LED32 = RGB LED (com. anode, rbg) [package="5 mm [THT]"]
  LED33 = RGB LED (com. anode, rbg) [package="5 mm [THT]"]
  R43 = Resistor [tolerance=±5% resistance=220 package=THT]
  R44 = Resistor [tolerance=±5% resistance=220 package=THT]
  IC4 = IC, DIP package, 16 pins [chip_label=IC]
  IC5 = IC, DIP package, 16 pins [chip_label=IC]
  C7 = Tantalum Capacitor [capacitance=1μF package="100 mil [THT, tantalum]"]
  C8 = Tantalum Capacitor [capacitance=1μF package="100 mil [THT, tantalum]"]
  C9 = Ceramic Capacitor [capacitance=100nF package="100 mil [THT, multilayer]"]
  C10 = Ceramic Capacitor [capacitance=100nF package="100 mil [THT, multilayer]"]
  LED34 = RGB LED (com. anode, rbg) [package="5 mm [THT]"]
  LED36 = RGB LED (com. anode, rbg) [package="5 mm [THT]"]
  R45 = Resistor [tolerance=±5% resistance=220 package=THT]
  IC6 = IC, DIP package, 16 pins [chip_label=IC]
  C11 = Tantalum Capacitor [capacitance=1μF package="100 mil [THT, tantalum]"]
  C12 = Ceramic Capacitor [capacitance=100nF package="100 mil [THT, multilayer]"]
  LED37 = RGB LED (com. anode, rbg) [package="5 mm [THT]"]
  LED38 = RGB LED (com. anode, rbg) [package="5 mm [THT]"]
  LED39 = RGB LED (com. anode, rbg) [package="5 mm [THT]"]
  R46 = Resistor [tolerance=±5% resistance=220 package=THT]
  IC7 = IC, DIP package, 16 pins [chip_label=IC]
  C13 = Tantalum Capacitor [capacitance=1μF package="100 mil [THT, tantalum]"]
  C14 = Ceramic Capacitor [capacitance=100nF package="100 mil [THT, multilayer]"]
  LED40 = RGB LED (com. anode, rbg) [package="5 mm [THT]"]
  LED41 = RGB LED (com. anode, rbg) [package="5 mm [THT]"]
  LED42 = RGB LED (com. anode, rbg) [package="5 mm [THT]"]
  LED43 = RGB LED (com. anode, rbg) [package="5 mm [THT]"]
  LED44 = RGB LED (com. anode, rbg) [package="5 mm [THT]"]
  R47 = Resistor [tolerance=±5% resistance=220 package=THT]
  R48 = Resistor [tolerance=±5% resistance=220 package=THT]
  IC8 = IC, DIP package, 16 pins [chip_label=IC]
  IC9 = IC, DIP package, 16 pins [chip_label=IC]
  C15 = Tantalum Capacitor [capacitance=1μF package="100 mil [THT, tantalum]"]
  C16 = Tantalum Capacitor [capacitance=1μF package="100 mil [THT, tantalum]"]
  C17 = Ceramic Capacitor [capacitance=100nF package="100 mil [THT, multilayer]"]
  C18 = Ceramic Capacitor [capacitance=100nF package="100 mil [THT, multilayer]"]
  LED45 = RGB LED (com. anode, rbg) [package="5 mm [THT]"]
  LED46 = RGB LED (com. anode, rbg) [package="5 mm [THT]"]
  LED47 = RGB LED (com. anode, rbg) [package="5 mm [THT]"]
  R49 = Resistor [tolerance=±5% resistance=220 package=THT]
  IC10 = IC, DIP package, 16 pins [chip_label=IC]
  C19 = Tantalum Capacitor [capacitance=1μF package="100 mil [THT, tantalum]"]
  C20 = Ceramic Capacitor [capacitance=100nF package="100 mil [THT, multilayer]"]
  LED48 = RGB LED (com. anode, rbg) [package="5 mm [THT]"]
  LED49 = RGB LED (com. anode, rbg) [package="5 mm [THT]"]
  LED50 = RGB LED (com. anode, rbg) [package="5 mm [THT]"]
  LED51 = RGB LED (com. anode, rbg) [package="5 mm [THT]"]
  LED52 = RGB LED (com. anode, rbg) [package="5 mm [THT]"]
  R50 = Resistor [tolerance=±5% resistance=220 package=THT]
  R51 = Resistor [tolerance=±5% resistance=220 package=THT]
  IC11 = IC, DIP package, 16 pins [chip_label=IC]
  IC12 = IC, DIP package, 16 pins [chip_label=IC]
  C21 = Tantalum Capacitor [capacitance=1μF package="100 mil [THT, tantalum]"]
  C22 = Tantalum Capacitor [capacitance=1μF package="100 mil [THT, tantalum]"]
  C23 = Ceramic Capacitor [capacitance=100nF package="100 mil [THT, multilayer]"]
  C24 = Ceramic Capacitor [capacitance=100nF package="100 mil [THT, multilayer]"]
  LED53 = RGB LED (com. anode, rbg) [package="5 mm [THT]"]
  LED54 = RGB LED (com. anode, rbg) [package="5 mm [THT]"]
  LED55 = RGB LED (com. anode, rbg) [package="5 mm [THT]"]
  R52 = Resistor [tolerance=±5% resistance=220 package=THT]
  IC13 = IC, DIP package, 16 pins [chip_label=IC]
  C25 = Tantalum Capacitor [capacitance=1μF package="100 mil [THT, tantalum]"]
  C26 = Ceramic Capacitor [capacitance=100nF package="100 mil [THT, multilayer]"]
  LED56 = RGB LED (com. anode, rbg) [package="5 mm [THT]"]
  LED57 = RGB LED (com. anode, rbg) [package="5 mm [THT]"]
  LED58 = RGB LED (com. anode, rbg) [package="5 mm [THT]"]
  LED59 = RGB LED (com. anode, rbg) [package="5 mm [THT]"]
  LED60 = RGB LED (com. anode, rbg) [package="5 mm [THT]"]
  R53 = Resistor [tolerance=±5% resistance=220 package=THT]
  R54 = Resistor [tolerance=±5% resistance=220 package=THT]
  IC14 = IC, DIP package, 16 pins [chip_label=IC]
  IC15 = IC, DIP package, 16 pins [chip_label=IC]
  C27 = Tantalum Capacitor [capacitance=1μF package="100 mil [THT, tantalum]"]
  C28 = Tantalum Capacitor [capacitance=1μF package="100 mil [THT, tantalum]"]
  C29 = Ceramic Capacitor [capacitance=100nF package="100 mil [THT, multilayer]"]
  C30 = Ceramic Capacitor [capacitance=100nF package="100 mil [THT, multilayer]"]
  LED61 = RGB LED (com. anode, rbg) [package="5 mm [THT]"]
  LED62 = RGB LED (com. anode, rbg) [package="5 mm [THT]"]
  LED63 = RGB LED (com. anode, rbg) [package="5 mm [THT]"]
  R55 = Resistor [tolerance=±5% resistance=220 package=THT]
  IC16 = IC, DIP package, 16 pins [chip_label=IC]
  C31 = Tantalum Capacitor [capacitance=1μF package="100 mil [THT, tantalum]"]
  C32 = Ceramic Capacitor [capacitance=100nF package="100 mil [THT, multilayer]"]
  LED64 = RGB LED (com. anode, rbg) [package="5 mm [THT]"]
  LED65 = RGB LED (com. anode, rbg) [package="5 mm [THT]"]
  LED66 = RGB LED (com. anode, rbg) [package="5 mm [THT]"]
  LED67 = RGB LED (com. anode, rbg) [package="5 mm [THT]"]
  LED68 = RGB LED (com. anode, rbg) [package="5 mm [THT]"]
  R56 = Resistor [tolerance=±5% resistance=220 package=THT]
  R57 = Resistor [tolerance=±5% resistance=220 package=THT]
  IC17 = IC, DIP package, 16 pins [chip_label=IC]
  IC18 = IC, DIP package, 16 pins [chip_label=IC]
  C33 = Tantalum Capacitor [capacitance=1μF package="100 mil [THT, tantalum]"]
  C34 = Tantalum Capacitor [capacitance=1μF package="100 mil [THT, tantalum]"]
  C35 = Ceramic Capacitor [capacitance=100nF package="100 mil [THT, multilayer]"]
  C36 = Ceramic Capacitor [capacitance=100nF package="100 mil [THT, multilayer]"]
  LED69 = RGB LED (com. anode, rbg) [package="5 mm [THT]"]
  LED70 = RGB LED (com. anode, rbg) [package="5 mm [THT]"]
  LED71 = RGB LED (com. anode, rbg) [package="5 mm [THT]"]
  R58 = Resistor [tolerance=±5% resistance=220 package=THT]
  IC19 = IC, DIP package, 16 pins [chip_label=IC]
  C37 = Tantalum Capacitor [capacitance=1μF package="100 mil [THT, tantalum]"]
  C38 = Ceramic Capacitor [capacitance=100nF package="100 mil [THT, multilayer]"]
  LED72 = RGB LED (com. anode, rbg) [package="5 mm [THT]"]
  LED73 = RGB LED (com. anode, rbg) [package="5 mm [THT]"]
  LED74 = RGB LED (com. anode, rbg) [package="5 mm [THT]"]
  LED75 = RGB LED (com. anode, rbg) [package="5 mm [THT]"]
  LED76 = RGB LED (com. anode, rbg) [package="5 mm [THT]"]
  R59 = Resistor [tolerance=±5% resistance=220 package=THT]
  R60 = Resistor [tolerance=±5% resistance=220 package=THT]
  IC20 = IC, DIP package, 16 pins [chip_label=IC]
  IC21 = IC, DIP package, 16 pins [chip_label=IC]
  C39 = Tantalum Capacitor [capacitance=1μF package="100 mil [THT, tantalum]"]
  C40 = Tantalum Capacitor [capacitance=1μF package="100 mil [THT, tantalum]"]
  C41 = Ceramic Capacitor [capacitance=100nF package="100 mil [THT, multilayer]"]
  C42 = Ceramic Capacitor [capacitance=100nF package="100 mil [THT, multilayer]"]

nets:
  N1: LED4.red_cathode, IC1.pin5
  N2: LED4.common_anode, LED18.common_anode, LED19.common_anode, J15.pin1, IC1.pin16, C1.+, C2.1, LED21.common_anode, LED23.common_anode, LED24.common_anode, IC2.pin16, C3.+, C4.1, LED25.common_anode, LED27.common_anode, IC3.pin16, C5.+, C6.1, LED28.common_anode, LED29.common_anode, LED30.common_anode, LED31.common_anode, LED32.common_anode, LED33.common_anode, IC4.pin16, IC5.pin16, C7.+, C8.+, C9.1, C10.1, LED34.common_anode, LED36.common_anode, IC6.pin16, C11.+, C12.1
  N3: LED4.blue_cathode, IC1.pin6
  N4: LED4.green_cathode, IC1.pin7
  N5: LED18.red_cathode, IC1.pin8
  N6: LED18.blue_cathode, IC1.pin9
  N7: LED18.green_cathode, IC1.pin10
  N8: LED19.red_cathode, IC1.pin11
  N9: LED19.blue_cathode, IC1.pin12
  N10: LED19.green_cathode, IC2.pin5
  N11: J15.pin2, R40.Pin_1, IC1.pin1, IC1.pin13, C1.-, C2.0, R41.Pin_1, IC2.pin1, IC2.pin13, C3.-, C4.0, R42.Pin_1, IC3.pin1, IC3.pin13, C5.-, C6.0, R43.Pin_1, R44.Pin_1, IC4.pin1, IC4.pin13, IC5.pin1, IC5.pin13, C7.-, C8.-, C9.0, C10.0, R45.Pin_1, IC6.pin1, IC6.pin13, C11.-, C12.0
  N12: J16.pin1, IC1.pin2
  N13: J16.pin2, IC1.pin3, IC2.pin3, IC3.pin3, IC4.pin3, IC5.pin3, IC6.pin3
  N14: J16.pin3, IC1.pin4, IC2.pin4, IC3.pin4, IC4.pin4, IC5.pin4, IC6.pin4
  N15: R40.Pin_0, IC1.pin15
  N16: IC1.pin14, IC2.pin2
  N17: LED21.red_cathode, IC2.pin12
  N18: LED21.blue_cathode, IC3.pin5
  N19: LED21.green_cathode, IC3.pin6
  N20: LED23.red_cathode, IC2.pin9
  N21: LED23.blue_cathode, IC2.pin10
  N22: LED23.green_cathode, IC2.pin11
  N23: LED24.red_cathode, IC2.pin6
  N24: LED24.blue_cathode, IC2.pin7
  N25: LED24.green_cathode, IC2.pin8
  N26: R41.Pin_0, IC2.pin15
  N27: IC2.pin14, IC3.pin2
  N28: LED25.red_cathode, IC3.pin7
  N29: LED25.blue_cathode, IC3.pin8
  N30: LED25.green_cathode, IC3.pin9
  N31: LED27.red_cathode, IC3.pin10
  N32: LED27.blue_cathode, IC3.pin11
  N33: LED27.green_cathode, IC3.pin12
  N34: R42.Pin_0, IC3.pin15
  N35: IC3.pin14, IC4.pin2
  N36: LED28.red_cathode, IC5.pin6
  N37: LED28.blue_cathode, IC5.pin7
  N38: LED28.green_cathode, IC5.pin8
  N39: LED29.red_cathode, IC4.pin11
  N40: LED29.blue_cathode, IC4.pin12
  N41: LED29.green_cathode, IC5.pin5
  N42: LED30.red_cathode, IC5.pin12
  N43: LED30.blue_cathode, IC6.pin5
  N44: LED30.green_cathode, IC6.pin6
  N45: LED31.red_cathode, IC4.pin8
  N46: LED31.blue_cathode, IC4.pin9
  N47: LED31.green_cathode, IC4.pin10
  N48: LED32.red_cathode, IC5.pin9
  N49: LED32.blue_cathode, IC5.pin10
  N50: LED32.green_cathode, IC5.pin11
  N51: LED33.red_cathode, IC4.pin5
  N52: LED33.blue_cathode, IC4.pin6
  N53: LED33.green_cathode, IC4.pin7
  N54: R43.Pin_0, IC4.pin15
  N55: R44.Pin_0, IC5.pin15
  N56: IC4.pin14, IC5.pin2
  N57: IC5.pin14, IC6.pin2
  N58: LED34.red_cathode, IC6.pin7
  N59: LED34.blue_cathode, IC6.pin8
  N60: LED34.green_cathode, IC6.pin9
  N61: LED36.red_cathode, IC6.pin10
  N62: LED36.blue_cathode, IC6.pin11
  N63: LED36.green_cathode, IC6.pin12
  N64: R45.Pin_0, IC6.pin15
  N65: LED37.red_cathode, IC8.pin5
  N66: LED37.common_anode, LED38.common_anode, LED39.common_anode, LED40.common_anode, LED41.common_anode, LED42.common_anode, LED43.common_anode, LED44.common_anode
  N67: LED37.blue_cathode, IC8.pin6
  N68: LED38.red_cathode, IC7.pin7
  N69: LED38.blue_cathode, IC7.pin8
  N70: LED38.green_cathode, IC7.pin9
  N71: LED39.red_cathode, IC7.pin10
  N72: LED39.blue_cathode, IC7.pin11
  N73: LED39.green_cathode, IC7.pin12
  N74: R46.Pin_0, IC7.pin15
  N75: R46.Pin_1, IC7.pin1, IC7.pin13
  N76: IC7.pin2, IC9.pin14
  N77: IC7.pin3, IC8.pin3, IC9.pin3
  N78: IC7.pin4, IC8.pin4, IC9.pin4
  N79: IC7.pin5, LED42.blue_cathode
  N80: IC7.pin6, LED42.green_cathode
  N81: IC7.pin16, C13.+, C14.1, IC8.pin16, IC9.pin16, C15.+, C16.+, C17.1, C18.1
  N82: C13.-, C14.0
  N83: LED40.red_cathode, IC9.pin6
  N84: LED40.blue_cathode, IC9.pin7
  N85: LED40.green_cathode, IC9.pin8
  N86: LED41.red_cathode, IC8.pin11
  N87: LED41.blue_cathode, IC8.pin12
  N88: LED41.green_cathode, IC9.pin5
  N89: LED42.red_cathode, IC9.pin12
  N90: LED43.red_cathode, IC8.pin8
  N91: LED43.blue_cathode, IC8.pin9
  N92: LED43.green_cathode, IC8.pin10
  N93: LED44.red_cathode, IC9.pin9
  N94: LED44.blue_cathode, IC9.pin10
  N95: LED44.green_cathode, IC9.pin11
  N96: R47.Pin_0, IC8.pin15
  N97: R47.Pin_1, IC8.pin1, IC8.pin13
  N98: R48.Pin_0, IC9.pin15
  N99: R48.Pin_1, IC9.pin1, IC9.pin13
  N100: IC8.pin14, IC9.pin2
  N101: C15.-, C17.0
  N102: C16.-, C18.0
  N103: LED45.red_cathode, IC11.pin5
  N104: LED45.common_anode, LED46.common_anode, LED47.common_anode, LED48.common_anode, LED49.common_anode, LED50.common_anode, LED51.common_anode, LED52.common_anode
  N105: LED45.blue_cathode, IC11.pin6
  N106: LED46.red_cathode, IC10.pin7
  N107: LED46.blue_cathode, IC10.pin8
  N108: LED46.green_cathode, IC10.pin9
  N109: LED47.red_cathode, IC10.pin10
  N110: LED47.blue_cathode, IC10.pin11
  N111: LED47.green_cathode, IC10.pin12
  N112: R49.Pin_0, IC10.pin15
  N113: R49.Pin_1, IC10.pin1, IC10.pin13
  N114: IC10.pin2, IC12.pin14
  N115: IC10.pin3, IC11.pin3, IC12.pin3
  N116: IC10.pin4, IC11.pin4, IC12.pin4
  N117: IC10.pin5, LED50.blue_cathode
  N118: IC10.pin6, LED50.green_cathode
  N119: IC10.pin16, C19.+, C20.1, IC11.pin16, IC12.pin16, C21.+, C22.+, C23.1, C24.1
  N120: C19.-, C20.0
  N121: LED48.red_cathode, IC12.pin6
  N122: LED48.blue_cathode, IC12.pin7
  N123: LED48.green_cathode, IC12.pin8
  N124: LED49.red_cathode, IC11.pin11
  N125: LED49.blue_cathode, IC11.pin12
  N126: LED49.green_cathode, IC12.pin5
  N127: LED50.red_cathode, IC12.pin12
  N128: LED51.red_cathode, IC11.pin8
  N129: LED51.blue_cathode, IC11.pin9
  N130: LED51.green_cathode, IC11.pin10
  N131: LED52.red_cathode, IC12.pin9
  N132: LED52.blue_cathode, IC12.pin10
  N133: LED52.green_cathode, IC12.pin11
  N134: R50.Pin_0, IC11.pin15
  N135: R50.Pin_1, IC11.pin1, IC11.pin13
  N136: R51.Pin_0, IC12.pin15
  N137: R51.Pin_1, IC12.pin1, IC12.pin13
  N138: IC11.pin14, IC12.pin2
  N139: C21.-, C23.0
  N140: C22.-, C24.0
  N141: LED53.red_cathode, IC14.pin5
  N142: LED53.common_anode, LED54.common_anode, LED55.common_anode, LED56.common_anode, LED57.common_anode, LED58.common_anode, LED59.common_anode, LED60.common_anode
  N143: LED53.blue_cathode, IC14.pin6
  N144: LED54.red_cathode, IC13.pin7
  N145: LED54.blue_cathode, IC13.pin8
  N146: LED54.green_cathode, IC13.pin9
  N147: LED55.red_cathode, IC13.pin10
  N148: LED55.blue_cathode, IC13.pin11
  N149: LED55.green_cathode, IC13.pin12
  N150: R52.Pin_0, IC13.pin15
  N151: R52.Pin_1, IC13.pin1, IC13.pin13
  N152: IC13.pin2, IC15.pin14
  N153: IC13.pin3, IC14.pin3, IC15.pin3
  N154: IC13.pin4, IC14.pin4, IC15.pin4
  N155: IC13.pin5, LED58.blue_cathode
  N156: IC13.pin6, LED58.green_cathode
  N157: IC13.pin16, C25.+, C26.1, IC14.pin16, IC15.pin16, C27.+, C28.+, C29.1, C30.1
  N158: C25.-, C26.0
  N159: LED56.red_cathode, IC15.pin6
  N160: LED56.blue_cathode, IC15.pin7
  N161: LED56.green_cathode, IC15.pin8
  N162: LED57.red_cathode, IC14.pin11
  N163: LED57.blue_cathode, IC14.pin12
  N164: LED57.green_cathode, IC15.pin5
  N165: LED58.red_cathode, IC15.pin12
  N166: LED59.red_cathode, IC14.pin8
  N167: LED59.blue_cathode, IC14.pin9
  N168: LED59.green_cathode, IC14.pin10
  N169: LED60.red_cathode, IC15.pin9
  N170: LED60.blue_cathode, IC15.pin10
  N171: LED60.green_cathode, IC15.pin11
  N172: R53.Pin_0, IC14.pin15
  N173: R53.Pin_1, IC14.pin1, IC14.pin13
  N174: R54.Pin_0, IC15.pin15
  N175: R54.Pin_1, IC15.pin1, IC15.pin13
  N176: IC14.pin14, IC15.pin2
  N177: C27.-, C29.0
  N178: C28.-, C30.0
  N179: LED61.red_cathode, IC17.pin5
  N180: LED61.common_anode, LED62.common_anode, LED63.common_anode, LED64.common_anode, LED65.common_anode, LED66.common_anode, LED67.common_anode, LED68.common_anode
  N181: LED61.blue_cathode, IC17.pin6
  N182: LED62.red_cathode, IC16.pin7
  N183: LED62.blue_cathode, IC16.pin8
  N184: LED62.green_cathode, IC16.pin9
  N185: LED63.red_cathode, IC16.pin10
  N186: LED63.blue_cathode, IC16.pin11
  N187: LED63.green_cathode, IC16.pin12
  N188: R55.Pin_0, IC16.pin15
  N189: R55.Pin_1, IC16.pin1, IC16.pin13
  N190: IC16.pin2, IC18.pin14
  N191: IC16.pin3, IC17.pin3, IC18.pin3
  N192: IC16.pin4, IC17.pin4, IC18.pin4
  N193: IC16.pin5, LED66.blue_cathode
  N194: IC16.pin6, LED66.green_cathode
  N195: IC16.pin16, C31.+, C32.1, IC17.pin16, IC18.pin16, C33.+, C34.+, C35.1, C36.1
  N196: C31.-, C32.0
  N197: LED64.red_cathode, IC18.pin6
  N198: LED64.blue_cathode, IC18.pin7
  N199: LED64.green_cathode, IC18.pin8
  N200: LED65.red_cathode, IC17.pin11
  N201: LED65.blue_cathode, IC17.pin12
  N202: LED65.green_cathode, IC18.pin5
  N203: LED66.red_cathode, IC18.pin12
  N204: LED67.red_cathode, IC17.pin8
  N205: LED67.blue_cathode, IC17.pin9
  N206: LED67.green_cathode, IC17.pin10
  N207: LED68.red_cathode, IC18.pin9
  N208: LED68.blue_cathode, IC18.pin10
  N209: LED68.green_cathode, IC18.pin11
  N210: R56.Pin_0, IC17.pin15
  N211: R56.Pin_1, IC17.pin1, IC17.pin13
  N212: R57.Pin_0, IC18.pin15
  N213: R57.Pin_1, IC18.pin1, IC18.pin13
  N214: IC17.pin14, IC18.pin2
  N215: C33.-, C35.0
  N216: C34.-, C36.0
  N217: LED69.red_cathode, IC20.pin5
  N218: LED69.common_anode, LED70.common_anode, LED71.common_anode, LED72.common_anode, LED73.common_anode, LED74.common_anode, LED75.common_anode, LED76.common_anode
  N219: LED69.blue_cathode, IC20.pin6
  N220: LED70.red_cathode, IC19.pin7
  N221: LED70.blue_cathode, IC19.pin8
  N222: LED70.green_cathode, IC19.pin9
  N223: LED71.red_cathode, IC19.pin10
  N224: LED71.blue_cathode, IC19.pin11
  N225: LED71.green_cathode, IC19.pin12
  N226: R58.Pin_0, IC19.pin15
  N227: R58.Pin_1, IC19.pin1, IC19.pin13
  N228: IC19.pin2, IC21.pin14
  N229: IC19.pin3, IC20.pin3, IC21.pin3
  N230: IC19.pin4, IC20.pin4, IC21.pin4
  N231: IC19.pin5, LED74.blue_cathode
  N232: IC19.pin6, LED74.green_cathode
  N233: IC19.pin16, C37.+, C38.1, IC20.pin16, IC21.pin16, C39.+, C40.+, C41.1, C42.1
  N234: C37.-, C38.0
  N235: LED72.red_cathode, IC21.pin6
  N236: LED72.blue_cathode, IC21.pin7
  N237: LED72.green_cathode, IC21.pin8
  N238: LED73.red_cathode, IC20.pin11
  N239: LED73.blue_cathode, IC20.pin12
  N240: LED73.green_cathode, IC21.pin5
  N241: LED74.red_cathode, IC21.pin12
  N242: LED75.red_cathode, IC20.pin8
  N243: LED75.blue_cathode, IC20.pin9
  N244: LED75.green_cathode, IC20.pin10
  N245: LED76.red_cathode, IC21.pin9
  N246: LED76.blue_cathode, IC21.pin10
  N247: LED76.green_cathode, IC21.pin11
  N248: R59.Pin_0, IC20.pin15
  N249: R59.Pin_1, IC20.pin1, IC20.pin13
  N250: R60.Pin_0, IC21.pin15
  N251: R60.Pin_1, IC21.pin1, IC21.pin13
  N252: IC20.pin14, IC21.pin2
  N253: C39.-, C41.0
  N254: C40.-, C42.0

notes:
  +
  -
  le
  clk
  sd
