# Fritzing sketch PCB Led Drivers (saved by Fritzing 0.9.1b)
circuit board: 3.15899cm x 40cm
breadboards: 1

parts:
  J15 = female pin header, 2 pins [form="♀ (female)"]
  J16 = female pin header, 3 pins [form="♀ (female)"]
  C5 = Tantalum Capacitor [capacitance=1μF package="100 mil [THT, tantalum]"]
  C6 = Ceramic Capacitor [capacitance=100nF package="100 mil [THT, multilayer]"]
  LED28 = RGB LED (com. anode, rbg) [package="5 mm [THT]"]
  LED29 = RGB LED (com. anode, rbg) [package="5 mm [THT]"]
  LED30 = RGB LED (com. anode, rbg) [package="5 mm [THT]"]
  LED31 = RGB LED (com. anode, rbg) [package="5 mm [THT]"]
  LED32 = RGB LED (com. anode, rbg) [package="5 mm [THT]"]
  LED33 = RGB LED (com. anode, rbg) [package="5 mm [THT]"]
  R43 = Resistor [tolerance=±5% resistance=220 package=THT]
  R44 = Resistor [tolerance=±5% resistance=220 package=THT]
  IC4 = IC, DIP package, 16 pins [chip_label=IC]
  IC5 = IC, DIP package, 16 pins [chip_label=IC]
  C7 = Tantalum Capacitor [capacitance=1μF package="100 mil [THT, tantalum]"]
  C8 = Tantalum Capacitor [capacitance=1μF package="100 mil [THT, tantalum]"]
  C9 = Ceramic Capacitor [capacitance=100nF package="100 mil [THT, multilayer]"]
  C10 = Ceramic Capacitor [capacitance=100nF package="100 mil [THT, multilayer]"]
  LED34 = RGB LED (com. anode, rbg) [package="5 mm [THT]"]
  LED36 = RGB LED (com. anode, rbg) [package="5 mm [THT]"]
  R45 = Resistor [tolerance=±5% resistance=220 package=THT]
  IC6 = IC, DIP package, 16 pins [chip_label=IC]
  LED37 = RGB LED (com. anode, rbg) [package="5 mm [THT]"]
  LED38 = RGB LED (com. anode, rbg) [package="5 mm [THT]"]
  LED39 = RGB LED (com. anode, rbg) [package="5 mm [THT]"]
  IC7 = IC, DIP package, 16 pins [chip_label=IC]
  R46 = Resistor [tolerance=±5% resistance=220 package=THT]
  C11 = Tantalum Capacitor [capacitance=1μF package="100 mil [THT, tantalum]"]
  C12 = Ceramic Capacitor [capacitance=100nF package="100 mil [THT, multilayer]"]
  LED40 = RGB LED (com. anode, rbg) [package="5 mm [THT]"]
  LED41 = RGB LED (com. anode, rbg) [package="5 mm [THT]"]
  LED42 = RGB LED (com. anode, rbg) [package="5 mm [THT]"]
  LED43 = RGB LED (com. anode, rbg) [package="5 mm [THT]"]
  LED44 = RGB LED (com. anode, rbg) [package="5 mm [THT]"]
  R47 = Resistor [tolerance=±5% resistance=220 package=THT]
  R48 = Resistor [tolerance=±5% resistance=220 package=THT]
  IC8 = IC, DIP package, 16 pins [chip_label=IC]
  IC9 = IC, DIP package, 16 pins [chip_label=IC]
  C13 = Tantalum Capacitor [capacitance=1μF package="100 mil [THT, tantalum]"]
  C14 = Tantalum Capacitor [capacitance=1μF package="100 mil [THT, tantalum]"]
  C15 = Ceramic Capacitor [capacitance=100nF package="100 mil [THT, multilayer]"]
  C16 = Ceramic Capacitor [capacitance=100nF package="100 mil [THT, multilayer]"]
  LED45 = RGB LED (com. anode, rbg) [package="5 mm [THT]"]
  LED46 = RGB LED (com. anode, rbg) [package="5 mm [THT]"]
  LED47 = RGB LED (com. anode, rbg) [package="5 mm [THT]"]
  LED48 = RGB LED (com. anode, rbg) [package="5 mm [THT]"]
  LED49 = RGB LED (com. anode, rbg) [package="5 mm [THT]"]
  LED50 = RGB LED (com. anode, rbg) [package="5 mm [THT]"]
  IC10 = IC, DIP package, 16 pins [chip_label=IC]
  IC11 = IC, DIP package, 16 pins [chip_label=IC]
  R49 = Resistor [tolerance=±5% resistance=220 package=THT]
  R50 = Resistor [tolerance=±5% resistance=220 package=THT]
  C17 = Tantalum Capacitor [capacitance=1μF package="100 mil [THT, tantalum]"]
  C18 = Tantalum Capacitor [capacitance=1μF package="100 mil [THT, tantalum]"]
  C19 = Ceramic Capacitor [capacitance=100nF package="100 mil [THT, multilayer]"]
  C20 = Ceramic Capacitor [capacitance=100nF package="100 mil [THT, multilayer]"]
  LED51 = RGB LED (com. anode, rbg) [package="5 mm [THT]"]
  LED52 = RGB LED (com. anode, rbg) [package="5 mm [THT]"]
  LED53 = RGB LED (com. anode, rbg) [package="5 mm [THT]"]
  LED54 = RGB LED (com. anode, rbg) [package="5 mm [THT]"]
  LED55 = RGB LED (com. anode, rbg) [package="5 mm [THT]"]
  LED56 = RGB LED (com. anode, rbg) [package="5 mm [THT]"]
  LED57 = RGB LED (com. anode, rbg) [package="5 mm [THT]"]
  LED58 = RGB LED (com. anode, rbg) [package="5 mm [THT]"]
  LED59 = RGB LED (com. anode, rbg) [package="5 mm [THT]"]
  LED60 = RGB LED (com. anode, rbg) [package="5 mm [THT]"]
  R51 = Resistor [tolerance=±5% resistance=220 package=THT]
  R52 = Resistor [tolerance=±5% resistance=220 package=THT]
  R53 = Resistor [tolerance=±5% resistance=220 package=THT]
  R54 = Resistor [tolerance=±5% resistance=220 package=THT]
  IC12 = IC, DIP package, 16 pins [chip_label=IC]
  IC13 = IC, DIP package, 16 pins [chip_label=IC]
  IC14 = IC, DIP package, 16 pins [chip_label=IC]
  IC15 = IC, DIP package, 16 pins [chip_label=IC]
  C21 = Tantalum Capacitor [capacitance=1μF package="100 mil [THT, tantalum]"]
  C22 = Tantalum Capacitor [capacitance=1μF package="100 mil [THT, tantalum]"]
  C23 = Tantalum Capacitor [capacitance=1μF package="100 mil [THT, tantalum]"]
  C24 = Tantalum Capacitor [capacitance=1μF package="100 mil [THT, tantalum]"]
  C25 = Ceramic Capacitor [capacitance=100nF package="100 mil [THT, multilayer]"]
  C26 = Ceramic Capacitor [capacitance=100nF package="100 mil [THT, multilayer]"]
  C27 = Ceramic Capacitor [capacitance=100nF package="100 mil [THT, multilayer]"]
  C28 = Ceramic Capacitor [capacitance=100nF package="100 mil [THT, multilayer]"]
  LED61 = RGB LED (com. anode, rbg) [package="5 mm [THT]"]
  LED62 = RGB LED (com. anode, rbg) [package="5 mm [THT]"]
  LED64 = RGB LED (com. anode, rbg) [package="5 mm [THT]"]
  LED65 = RGB LED (com. anode, rbg) [package="5 mm [THT]"]
  LED66 = RGB LED (com. anode, rbg) [package="5 mm [THT]"]
  LED67 = RGB LED (com. anode, rbg) [package="5 mm [THT]"]
  LED68 = RGB LED (com. anode, rbg) [package="5 mm [THT]"]
  LED69 = RGB LED (com. anode, rbg) [package="5 mm [THT]"]
  LED71 = RGB LED (com. anode, rbg) [package="5 mm [THT]"]
  LED72 = RGB LED (com. anode, rbg) [package="5 mm [THT]"]
  IC16 = IC, DIP package, 16 pins [chip_label=IC]
  IC17 = IC, DIP package, 16 pins [chip_label=IC]
  IC18 = IC, DIP package, 16 pins [chip_label=IC]
  R55 = Resistor [tolerance=±5% resistance=220 package=THT]
  R56 = Resistor [tolerance=±5% resistance=220 package=THT]
  R57 = Resistor [tolerance=±5% resistance=220 package=THT]
  C29 = Tantalum Capacitor [capacitance=1μF package="100 mil [THT, tantalum]"]
  C30 = Tantalum Capacitor [capacitance=1μF package="100 mil [THT, tantalum]"]
  C31 = Tantalum Capacitor [capacitance=1μF package="100 mil [THT, tantalum]"]
  C32 = Tantalum Capacitor [capacitance=1μF package="100 mil [THT, tantalum]"]
  C33 = Ceramic Capacitor [capacitance=100nF package="100 mil [THT, multilayer]"]
  C34 = Ceramic Capacitor [capacitance=100nF package="100 mil [THT, multilayer]"]
  C35 = Ceramic Capacitor [capacitance=100nF package="100 mil [THT, multilayer]"]
  C36 = Ceramic Capacitor [capacitance=100nF package="100 mil [THT, multilayer]"]
  LED73 = RGB LED (com. anode, rbg) [package="5 mm [THT]"]
  LED74 = RGB LED (com. anode, rbg) [package="5 mm [THT]"]
  LED75 = RGB LED (com. anode, rbg) [package="5 mm [THT]"]
  LED76 = RGB LED (com. anode, rbg) [package="5 mm [THT]"]
  LED77 = RGB LED (com. anode, rbg) [package="5 mm [THT]"]
  LED78 = RGB LED (com. anode, rbg) [package="5 mm [THT]"]
  LED79 = RGB LED (com. anode, rbg) [package="5 mm [THT]"]
  LED80 = RGB LED (com. anode, rbg) [package="5 mm [THT]"]
  LED81 = RGB LED (com. anode, rbg) [package="5 mm [THT]"]
  LED83 = RGB LED (com. anode, rbg) [package="5 mm [THT]"]
  LED84 = RGB LED (com. anode, rbg) [package="5 mm [THT]"]
  LED85 = RGB LED (com. anode, rbg) [package="5 mm [THT]"]
  LED86 = RGB LED (com. anode, rbg) [package="5 mm [THT]"]
  LED87 = RGB LED (com. anode, rbg) [package="5 mm [THT]"]
  LED88 = RGB LED (com. anode, rbg) [package="5 mm [THT]"]
  LED89 = RGB LED (com. anode, rbg) [package="5 mm [THT]"]
  LED90 = RGB LED (com. anode, rbg) [package="5 mm [THT]"]
  LED91 = RGB LED (com. anode, rbg) [package="5 mm [THT]"]
  LED92 = RGB LED (com. anode, rbg) [package="5 mm [THT]"]
  R59 = Resistor [tolerance=±5% resistance=220 package=THT]
  R60 = Resistor [tolerance=±5% resistance=220 package=THT]
  R61 = Resistor [tolerance=±5% resistance=220 package=THT]
  R62 = Resistor [tolerance=±5% resistance=220 package=THT]
  R63 = Resistor [tolerance=±5% resistance=220 package=THT]
  R64 = Resistor [tolerance=±5% resistance=220 package=THT]
  R65 = Resistor [tolerance=±5% resistance=220 package=THT]
  R66 = Resistor [tolerance=±5% resistance=220 package=THT]
  IC20 = IC, DIP package, 16 pins [chip_label=IC]
  IC21 = IC, DIP package, 16 pins [chip_label=IC]
  IC22 = IC, DIP package, 16 pins [chip_label=IC]
  IC23 = IC, DIP package, 16 pins [chip_label=IC]
  IC24 = IC, DIP package, 16 pins [chip_label=IC]
  IC25 = IC, DIP package, 16 pins [chip_label=IC]
  IC26 = IC, DIP package, 16 pins [chip_label=IC]
  IC27 = IC, DIP package, 16 pins [chip_label=IC]
  C37 = Tantalum Capacitor [capacitance=1μF package="100 mil [THT, tantalum]"]
  C38 = Tantalum Capacitor [capacitance=1μF package="100 mil [THT, tantalum]"]
  C39 = Tantalum Capacitor [capacitance=1μF package="100 mil [THT, tantalum]"]
  C40 = Tantalum Capacitor [capacitance=1μF package="100 mil [THT, tantalum]"]
  C41 = Tantalum Capacitor [capacitance=1μF package="100 mil [THT, tantalum]"]
  C42 = Tantalum Capacitor [capacitance=1μF package="100 mil [THT, tantalum]"]
  C43 = Tantalum Capacitor [capacitance=1μF package="100 mil [THT, tantalum]"]
  C44 = Tantalum Capacitor [capacitance=1μF package="100 mil [THT, tantalum]"]
  C45 = Ceramic Capacitor [capacitance=100nF package="100 mil [THT, multilayer]"]
  C46 = Ceramic Capacitor [capacitance=100nF package="100 mil [THT, multilayer]"]
  C47 = Ceramic Capacitor [capacitance=100nF package="100 mil [THT, multilayer]"]
  C48 = Ceramic Capacitor [capacitance=100nF package="100 mil [THT, multilayer]"]
  C49 = Ceramic Capacitor [capacitance=100nF package="100 mil [THT, multilayer]"]
  C50 = Ceramic Capacitor [capacitance=100nF package="100 mil [THT, multilayer]"]
  C51 = Ceramic Capacitor [capacitance=100nF package="100 mil [THT, multilayer]"]
  C52 = Ceramic Capacitor [capacitance=100nF package="100 mil [THT, multilayer]"]
  J17 = female pin header, 2 pins [form="♀ (female)"]
  R67 = Resistor [tolerance=±5% resistance=220 package=THT]
  R68 = Resistor [tolerance=±5% resistance=220 package=THT]

nets:
  N1: J15.pin1, C5.+, C6.0, LED28.common_anode, LED29.common_anode, LED30.common_anode, LED31.common_anode, LED32.common_anode, LED33.common_anode, IC4.pin16, IC5.pin16, C7.-, C8.-, C9.1, C10.1, LED34.common_anode, LED36.common_anode, IC6.pin16, LED37.common_anode, LED38.common_anode, LED39.common_anode, IC7.pin16, C11.+, C12.0, LED40.common_anode, LED41.common_anode, LED42.common_anode, LED43.common_anode, LED44.common_anode, IC8.pin16, IC9.pin16, C13.-, C14.-, C15.1, C16.1, LED45.common_anode, LED46.common_anode, LED47.common_anode, LED48.common_anode, LED49.common_anode, LED50.common_anode, IC10.pin16, IC11.pin16, C17.+, C18.+, C19.0, C20.0, LED51.common_anode, LED52.common_anode, LED53.common_anode, LED54.common_anode, LED55.common_anode, LED56.common_anode, LED57.common_anode, LED58.common_anode, LED59.common_anode, LED60.common_anode, IC12.pin16, IC13.pin16, IC14.pin16, IC15.pin16, C21.-, C22.-, C23.-, C24.-, C25.1, C26.1, C27.1, C28.1, LED61.common_anode, LED62.common_anode, LED64.common_anode, LED65.common_anode, LED66.common_anode, LED67.common_anode, LED68.common_anode, LED69.common_anode, LED71.common_anode, LED72.common_anode, IC16.pin16, IC17.pin16, IC18.pin16, C29.+, C30.+, C31.+, C32.+, C33.0, C34.0, C35.0, C36.0, LED73.common_anode, LED74.common_anode, LED75.common_anode, LED76.common_anode, LED77.common_anode, LED78.common_anode, LED79.common_anode, LED80.common_anode, LED81.common_anode, LED83.common_anode, LED84.common_anode, LED85.common_anode, LED86.common_anode, LED87.common_anode, LED88.common_anode, LED89.common_anode, LED90.common_anode, LED91.common_anode, LED92.common_anode, IC20.pin16, IC21.pin16, IC22.pin16, IC23.pin16, IC24.pin16, IC25.pin16, IC26.pin16, IC27.pin16, C37.-, C38.-, C39.-, C40.-, C41.-, C42.-, C43.+, C44.-, C45.1, C46.1, C47.1, C48.1, C49.1, C50.1, C51.1, C52.1, J17.pin2
  N2: J15.pin2, C5.-, C6.1, R43.Pin_1, R44.Pin_1, IC4.pin1, IC4.pin13, IC5.pin1, IC5.pin13, C7.+, C8.+, C9.0, C10.0, R45.Pin_1, IC6.pin1, IC6.pin13, IC7.pin1, IC7.pin13, R46.Pin_1, C11.-, C12.1, R47.Pin_1, R48.Pin_1, IC8.pin1, IC8.pin13, IC9.pin1, IC9.pin13, C13.+, C14.+, C15.0, C16.0, IC10.pin1, IC10.pin13, IC11.pin1, IC11.pin13, R49.Pin_1, R50.Pin_1, C17.-, C18.-, C19.1, C20.1, R51.Pin_1, R52.Pin_1, R53.Pin_1, R54.Pin_1, IC12.pin1, IC12.pin13, IC13.pin1, IC13.pin13, IC14.pin1, IC14.pin13, IC15.pin1, IC15.pin13, C21.+, C22.+, C23.+, C24.+, C25.0, C26.0, C27.0, C28.0, IC16.pin1, IC16.pin13, IC17.pin1, IC17.pin13, IC18.pin1, IC18.pin13, R55.Pin_1, R56.Pin_1, R57.Pin_1, C29.-, C30.-, C31.-, C32.-, C33.1, C34.1, C35.1, C36.1, R59.Pin_1, R60.Pin_1, R61.Pin_1, R62.Pin_1, R63.Pin_1, R64.Pin_1, R65.Pin_1, R66.Pin_1, IC20.pin1, IC20.pin13, IC21.pin1, IC21.pin13, IC22.pin1, IC22.pin13, IC23.pin1, IC23.pin13, IC24.pin1, IC24.pin13, IC25.pin1, IC25.pin13, IC26.pin1, IC26.pin13, IC27.pin1, IC27.pin13, C37.+, C38.+, C39.+, C40.+, C41.+, C42.+, C44.+, C45.0, C46.0, C47.0, C48.0, C49.0, C51.0, C52.0
  N3: J16.pin1, IC4.pin2
  N4: J16.pin2, IC4.pin3, IC5.pin3, IC6.pin3, IC7.pin3, IC8.pin3, IC9.pin3, IC10.pin3, IC11.pin3, IC12.pin3, IC13.pin3, IC14.pin3, IC15.pin3, IC16.pin3, IC17.pin3, IC18.pin3, IC20.pin3, IC21.pin3, IC22.pin3, IC23.pin3, IC24.pin3, IC25.pin3, IC26.pin3, IC27.pin3, R68.Pin_1
  N5: J16.pin3, IC4.pin4, IC5.pin4, IC6.pin4, IC7.pin4, IC8.pin4, IC9.pin4, IC10.pin4, IC11.pin4, IC12.pin4, IC13.pin4, IC14.pin4, IC15.pin4, IC16.pin4, IC17.pin4, IC18.pin4, IC20.pin4, IC21.pin4, IC22.pin4, IC23.pin4, IC24.pin4, IC25.pin4, IC26.pin4, IC27.pin4, R67.Pin_1
  N6: LED28.red_cathode, IC5.pin6
  N7: LED28.blue_cathode, IC5.pin7
  N8: LED28.green_cathode, IC5.pin8
  N9: LED29.red_cathode, IC4.pin11
  N10: LED29.blue_cathode, IC4.pin12
  N11: LED29.green_cathode, IC5.pin5
  N12: LED30.red_cathode, IC5.pin12
  N13: LED30.blue_cathode, IC6.pin5
  N14: LED30.green_cathode, IC6.pin6
  N15: LED31.red_cathode, IC4.pin8
  N16: LED31.blue_cathode, IC4.pin9
  N17: LED31.green_cathode, IC4.pin10
  N18: LED32.red_cathode, IC5.pin9
  N19: LED32.blue_cathode, IC5.pin10
  N20: LED32.green_cathode, IC5.pin11
  N21: LED33.red_cathode, IC4.pin5
  N22: LED33.blue_cathode, IC4.pin6
  N23: LED33.green_cathode, IC4.pin7
  N24: R43.Pin_0, IC4.pin15
  N25: R44.Pin_0, IC5.pin15
  N26: IC4.pin14, IC5.pin2
  N27: IC5.pin14, IC6.pin2
  N28: LED34.red_cathode, IC6.pin7
  N29: LED34.blue_cathode, IC6.pin8
  N30: LED34.green_cathode, IC6.pin9
  N31: LED36.red_cathode, IC6.pin10
  N32: LED36.blue_cathode, IC6.pin11
  N33: LED36.green_cathode, IC6.pin12
  N34: R45.Pin_0, IC6.pin15
  N35: IC6.pin14, IC8.pin2
  N36: LED37.red_cathode, IC7.pin7
  N37: LED37.blue_cathode, IC7.pin8
  N38: LED37.green_cathode, IC7.pin9
  N39: LED38.red_cathode, IC8.pin5
  N40: LED38.blue_cathode, IC8.pin6
  N41: LED38.green_cathode, IC8.pin7
  N42: LED39.red_cathode, IC7.pin10
  N43: LED39.blue_cathode, IC7.pin11
  N44: LED39.green_cathode, IC7.pin12
  N45: IC7.pin2, IC9.pin14
  N46: IC7.pin5, LED42.blue_cathode
  N47: IC7.pin6, LED42.green_cathode
  N48: IC7.pin14, IC12.pin2
  N49: IC7.pin15, R46.Pin_0
  N50: LED40.red_cathode, IC9.pin6
  N51: LED40.blue_cathode, IC9.pin7
  N52: LED40.green_cathode, IC9.pin8
  N53: LED41.red_cathode, IC8.pin11
  N54: LED41.blue_cathode, IC8.pin12
  N55: LED41.green_cathode, IC9.pin5
  N56: LED42.red_cathode, IC9.pin12
  N57: LED43.red_cathode, IC8.pin8
  N58: LED43.blue_cathode, IC8.pin9
  N59: LED43.green_cathode, IC8.pin10
  N60: LED44.red_cathode, IC9.pin9
  N61: LED44.blue_cathode, IC9.pin10
  N62: LED44.green_cathode, IC9.pin11
  N63: R47.Pin_0, IC8.pin15
  N64: R48.Pin_0, IC9.pin15
  N65: IC8.pin14, IC9.pin2
  N66: LED45.red_cathode, IC10.pin7
  N67: LED45.blue_cathode, IC10.pin8
  N68: LED45.green_cathode, IC10.pin9
  N69: LED46.red_cathode, IC11.pin7
  N70: LED46.blue_cathode, IC11.pin8
  N71: LED46.green_cathode, IC11.pin9
  N72: LED47.red_cathode, IC12.pin5
  N73: LED47.blue_cathode, IC12.pin6
  N74: LED47.green_cathode, IC12.pin7
  N75: LED48.red_cathode, IC13.pin5
  N76: LED48.blue_cathode, IC13.pin6
  N77: LED48.green_cathode, IC13.pin7
  N78: LED49.red_cathode, IC10.pin10
  N79: LED49.blue_cathode, IC10.pin11
  N80: LED49.green_cathode, IC10.pin12
  N81: LED50.red_cathode, IC11.pin10
  N82: LED50.blue_cathode, IC11.pin11
  N83: LED50.green_cathode, IC11.pin12
  N84: IC10.pin2, IC14.pin14
  N85: IC10.pin5, LED55.blue_cathode
  N86: IC10.pin6, LED55.green_cathode
  N87: IC10.pin14, IC13.pin2
  N88: IC10.pin15, R49.Pin_0
  N89: IC11.pin2, IC15.pin14
  N90: IC11.pin5, LED56.blue_cathode
  N91: IC11.pin6, LED56.green_cathode
  N92: IC11.pin14, IC20.pin2
  N93: IC11.pin15, R50.Pin_0
  N94: LED51.red_cathode, IC14.pin6
  N95: LED51.blue_cathode, IC14.pin7
  N96: LED51.green_cathode, IC14.pin8
  N97: LED52.red_cathode, IC15.pin6
  N98: LED52.blue_cathode, IC15.pin7
  N99: LED52.green_cathode, IC15.pin8
  N100: LED53.red_cathode, IC12.pin11
  N101: LED53.blue_cathode, IC12.pin12
  N102: LED53.green_cathode, IC14.pin5
  N103: LED54.red_cathode, IC13.pin11
  N104: LED54.blue_cathode, IC13.pin12
  N105: LED54.green_cathode, IC15.pin5
  N106: LED55.red_cathode, IC14.pin12
  N107: LED56.red_cathode, IC15.pin12
  N108: LED57.red_cathode, IC12.pin8
  N109: LED57.blue_cathode, IC12.pin9
  N110: LED57.green_cathode, IC12.pin10
  N111: LED58.red_cathode, IC13.pin8
  N112: LED58.blue_cathode, IC13.pin9
  N113: LED58.green_cathode, IC13.pin10
  N114: LED59.red_cathode, IC14.pin9
  N115: LED59.blue_cathode, IC14.pin10
  N116: LED59.green_cathode, IC14.pin11
  N117: LED60.red_cathode, IC15.pin9
  N118: LED60.blue_cathode, IC15.pin10
  N119: LED60.green_cathode, IC15.pin11
  N120: R51.Pin_0, IC12.pin15
  N121: R52.Pin_0, IC13.pin15
  N122: R53.Pin_0, IC14.pin15
  N123: R54.Pin_0, IC15.pin15
  N124: IC12.pin14, IC14.pin2
  N125: IC13.pin14, IC15.pin2
  N126: LED61.red_cathode, IC16.pin7
  N127: LED61.blue_cathode, IC16.pin8
  N128: LED61.green_cathode, IC16.pin9
  N129: LED62.red_cathode, IC18.pin7
  N130: LED62.blue_cathode, IC18.pin8
  N131: LED62.green_cathode, IC18.pin9
  N132: LED64.red_cathode, IC17.pin7
  N133: LED64.blue_cathode, IC17.pin8
  N134: LED64.green_cathode, IC17.pin9
  N135: LED65.red_cathode, IC20.pin5
  N136: LED65.blue_cathode, IC20.pin6
  N137: LED65.green_cathode, IC20.pin7
  N138: LED66.red_cathode, IC21.pin5
  N139: LED66.blue_cathode, IC21.pin6
  N140: LED66.green_cathode, IC21.pin7
  N141: LED67.red_cathode, IC22.pin5
  N142: LED67.blue_cathode, IC22.pin6
  N143: LED67.green_cathode, IC22.pin7
  N144: LED68.red_cathode, IC23.pin5
  N145: LED68.blue_cathode, IC23.pin6
  N146: LED68.green_cathode, IC23.pin7
  N147: LED69.red_cathode, IC16.pin10
  N148: LED69.blue_cathode, IC16.pin11
  N149: LED69.green_cathode, IC16.pin12
  N150: LED71.red_cathode, IC17.pin10
  N151: LED71.blue_cathode, IC17.pin11
  N152: LED71.green_cathode, IC17.pin12
  N153: LED72.red_cathode, IC18.pin10
  N154: LED72.blue_cathode, IC18.pin11
  N155: LED72.green_cathode, IC18.pin12
  N156: IC16.pin2, IC24.pin14
  N157: IC16.pin5, LED81.blue_cathode
  N158: IC16.pin6, LED81.green_cathode
  N159: IC16.pin14, IC23.pin2
  N160: IC16.pin15, R55.Pin_0
  N161: IC17.pin2, IC26.pin14
  N162: IC17.pin5, LED84.blue_cathode
  N163: IC17.pin6, LED84.green_cathode
  N164: IC17.pin14, IC21.pin2
  N165: IC17.pin15, R56.Pin_0
  N166: IC18.pin2, IC27.pin14
  N167: IC18.pin5, LED83.blue_cathode
  N168: IC18.pin6, LED83.green_cathode
  N169: IC18.pin14, IC22.pin2
  N170: IC18.pin15, R57.Pin_0
  N171: LED73.red_cathode, IC24.pin6
  N172: LED73.blue_cathode, IC24.pin7
  N173: LED73.green_cathode, IC24.pin8
  N174: LED74.red_cathode, IC25.pin6
  N175: LED74.blue_cathode, IC25.pin7
  N176: LED74.green_cathode, IC25.pin8
  N177: LED75.red_cathode, IC26.pin6
  N178: LED75.blue_cathode, IC26.pin7
  N179: LED75.green_cathode, IC26.pin8
  N180: LED76.red_cathode, IC27.pin6
  N181: LED76.blue_cathode, IC27.pin7
  N182: LED76.green_cathode, IC27.pin8
  N183: LED77.red_cathode, IC20.pin11
  N184: LED77.blue_cathode, IC20.pin12
  N185: LED77.green_cathode, IC24.pin5
  N186: LED78.red_cathode, IC23.pin11
  N187: LED78.blue_cathode, IC23.pin12
  N188: LED78.green_cathode, IC26.pin5
  N189: LED79.red_cathode, IC22.pin11
  N190: LED79.blue_cathode, IC22.pin12
  N191: LED79.green_cathode, IC25.pin5
  N192: LED80.red_cathode, IC21.pin11
  N193: LED80.blue_cathode, IC21.pin12
  N194: LED80.green_cathode, IC27.pin5
  N195: LED81.red_cathode, IC24.pin12
  N196: LED83.red_cathode, IC27.pin12
  N197: LED84.red_cathode, IC26.pin12
  N198: LED85.red_cathode, IC20.pin8
  N199: LED85.blue_cathode, IC20.pin9
  N200: LED85.green_cathode, IC20.pin10
  N201: LED86.red_cathode, IC23.pin8
  N202: LED86.blue_cathode, IC23.pin9
  N203: LED86.green_cathode, IC23.pin10
  N204: LED87.red_cathode, IC22.pin8
  N205: LED87.blue_cathode, IC22.pin9
  N206: LED87.green_cathode, IC22.pin10
  N207: LED88.red_cathode, IC21.pin8
  N208: LED88.blue_cathode, IC21.pin9
  N209: LED88.green_cathode, IC21.pin10
  N210: LED89.red_cathode, IC24.pin9
  N211: LED89.blue_cathode, IC24.pin10
  N212: LED89.green_cathode, IC24.pin11
  N213: LED90.red_cathode, IC27.pin9
  N214: LED90.blue_cathode, IC27.pin10
  N215: LED90.green_cathode, IC27.pin11
  N216: LED91.red_cathode, IC25.pin9
  N217: LED91.blue_cathode, IC25.pin10
  N218: LED91.green_cathode, IC25.pin11
  N219: LED92.red_cathode, IC26.pin9
  N220: LED92.blue_cathode, IC26.pin10
  N221: LED92.green_cathode, IC26.pin11
  N222: R59.Pin_0, IC20.pin15
  N223: R60.Pin_0, IC22.pin15
  N224: R61.Pin_0, IC23.pin15
  N225: R62.Pin_0, IC21.pin15
  N226: R63.Pin_0, IC24.pin15
  N227: R64.Pin_0, IC25.pin15
  N228: R65.Pin_0, IC26.pin15
  N229: R66.Pin_0, IC27.pin15
  N230: IC20.pin14, IC24.pin2
  N231: IC21.pin14, IC27.pin2
  N232: IC22.pin14, IC25.pin2
  N233: IC23.pin14, IC26.pin2
  N234: C43.-, C50.0, J17.pin1, R67.Pin_0, R68.Pin_0

notes:
  +
  -
  le
  clk
  sd
